# Fritzing sketch bach (saved by Fritzing 0.9.4)
breadboards: 1

parts:
  MH-ET_LIVE_ESP32_DEVKIT1 = MH-ET LIVE ESP32 DEVKIT 38 pins
  Composant1 = Adafruit VS1053 Codec + MicroSD Breakout - MP3/WAV/MIDI/OGG [part_number="Adafruit #1381"]
  LCD2 = LCD screen
  LCM1602_IIC2 = LCM1602 IIC [part_number="LCM1602 IIC" chip_label="LCM1602 IIC" package="DIP (Dual Inline) [THT]"]
  R1 = Rotary Potentiometer (Small) [maximum_resistance=100kΩ package=THT]
  U1 = 74x125 [part_number=74x125 package="DIP (Dual Inline) [THT]"]
  Composant2 = 74x125 [part_number=74x125 package="DIP (Dual Inline) [THT]"]  # not connected
  U1_1 = 74x125 [part_number=74x125 package="DIP (Dual Inline) [THT]"]  # not connected
  U1_2 = 74x125 [part_number=74x125 package="DIP (Dual Inline) [THT]"]  # not connected
  U1_3 = 74x125 [part_number=74x125 package="DIP (Dual Inline) [THT]"]  # not connected
  U1_4 = 74x125 [part_number=74x125 package="DIP (Dual Inline) [THT]"]  # not connected
  TRS1 = SUYIN Audio Jack (TRS) 3.5mm [package="SUYIN [THT]"]
  NEOPIXEL1 = Neopixel Strip -- White (30/m) [part_number=1376]
  R2 = Resistor [tolerance=±5% resistance=220 package="0402 [SMD]"]
  C1 = Capacitor Polarized [package=cpol-radial-10uf-25v]
  R3 = Resistor [tolerance=±5% resistance=220 package=THT]

nets:
  N1: MH-ET_LIVE_ESP32_DEVKIT1.3V3, Composant1.GPIO1, R1.leg1
  N2: MH-ET_LIVE_ESP32_DEVKIT1.SVP, R1.wiper, R3.Pin_0
  5V: MH-ET_LIVE_ESP32_DEVKIT1.5V, Composant1.VIN, LCM1602_IIC2.VCC, U1.connector13, NEOPIXEL1.+5V, C1.+
  GND: MH-ET_LIVE_ESP32_DEVKIT1.GND#64, LCM1602_IIC2.GND, U1.connector0, TRS1.Sleeve, NEOPIXEL1.GND, C1.-, R3.Pin_1
  N3: MH-ET_LIVE_ESP32_DEVKIT1.TXD0, Composant1.RX_5V
  N4: MH-ET_LIVE_ESP32_DEVKIT1.IO4, Composant1.RST_5V
  N5: MH-ET_LIVE_ESP32_DEVKIT1.IO2, U1.connector1
  N6: MH-ET_LIVE_ESP32_DEVKIT1.SD0, LCM1602_IIC2.SDA
  N7: MH-ET_LIVE_ESP32_DEVKIT1.SCK, LCM1602_IIC2.SCL
  N8: Composant1.R_OUT, U1.connector6, TRS1.Tip
  N9: Composant1.L_OUT, TRS1.Ring
  N10: Composant1.AGND, R2.Pin_0
  N11: Composant1.MIC_N, R2.Pin_1
  VSS: LCD2.VSS, LCM1602_IIC2.VSS
  VDD: LCD2.VDD, LCM1602_IIC2.VDD
  N12: LCD2.V0, LCM1602_IIC2.V0
  N13: LCD2.RS, LCM1602_IIC2.RS
  N14: LCD2.R/W, LCM1602_IIC2.RW
  N15: LCD2.E, LCM1602_IIC2.E
  N16: LCD2.DB0, LCM1602_IIC2.D0
  N17: LCD2.DB1, LCM1602_IIC2.D1
  N18: LCD2.DB2, LCM1602_IIC2.D2
  N19: LCD2.DB3, LCM1602_IIC2.D3
  N20: LCD2.DB4, LCM1602_IIC2.D4
  N21: LCD2.DB5, LCM1602_IIC2.D5
  N22: LCD2.DB6, LCM1602_IIC2.D6
  N23: LCD2.DB7, LCM1602_IIC2.D7
  N24: LCD2.LED+, LCM1602_IIC2.A
  N25: LCD2.LED-, LCM1602_IIC2.K
  N26: LCM1602_IIC2.LED_A, LCM1602_IIC2.LED_B
  N27: U1.connector2, NEOPIXEL1.Din
  N28: U1.connector8, U1.connector10

custom parts:
  MH-ET LIVE ESP32 DEVKIT 38 pins: http://mh.nodebb.com/topic/2/mh-et-live-esp32-devkit
  Adafruit VS1053 Codec + MicroSD Breakout - MP3/WAV/MIDI/OGG: This breakout board is the ultimate companion for the VLSI VS1053B DSP codec chip. The VS1053 can decode a wide variety of audio formats such as MP3, AAC, Ogg Vorbis, WMA, MIDI, FLAC, WAV (PCM and ADPCM). It can also be used to record audio in both PCM (WAV) and compressed Ogg Vorbis. You can do all sorts of stuff with the audio as well such as adjusting bass, treble, and volume digitally.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
  LCM1602 IIC: I2C-Module to use a 1602 or 2004 LCD on with the wire.h libory Serial LCD Modul
  74x125: 74x125 quad tristate buffer active low enable. The 74ahc125 variety is useful as a level translator as the inputs are 5V tolorant when run with a VCC of 3.3V (and will thus take a 5V signal in and provide a 3.3V signal out.) As well this part uses schematic subparts so you can drag each of the 4 gates to a different place in schematic view. Note having many (around 10 or more) subpart parts in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
  74x125: 74x125 quad tristate buffer active low enable. The 74ahc125 variety is useful as a level translator as the inputs are 5V tolorant when run with a VCC of 3.3V (and will thus take a 5V signal in and provide a 3.3V signal out.) As well this part uses schematic subparts so you can drag each of the 4 gates to a different place in schematic view. Note having many (around 10 or more) subpart parts in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
  74x125: 74x125 quad tristate buffer active low enable. The 74ahc125 variety is useful as a level translator as the inputs are 5V tolorant when run with a VCC of 3.3V (and will thus take a 5V signal in and provide a 3.3V signal out.) As well this part uses schematic subparts so you can drag each of the 4 gates to a different place in schematic view. Note having many (around 10 or more) subpart parts in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
  74x125: 74x125 quad tristate buffer active low enable. The 74ahc125 variety is useful as a level translator as the inputs are 5V tolorant when run with a VCC of 3.3V (and will thus take a 5V signal in and provide a 3.3V signal out.) As well this part uses schematic subparts so you can drag each of the 4 gates to a different place in schematic view. Note having many (around 10 or more) subpart parts in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
  74x125: 74x125 quad tristate buffer active low enable. The 74ahc125 variety is useful as a level translator as the inputs are 5V tolorant when run with a VCC of 3.3V (and will thus take a 5V signal in and provide a 3.3V signal out.) As well this part uses schematic subparts so you can drag each of the 4 gates to a different place in schematic view. Note having many (around 10 or more) subpart parts in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
  74x125: 74x125 quad tristate buffer active low enable. The 74ahc125 variety is useful as a level translator as the inputs are 5V tolorant when run with a VCC of 3.3V (and will thus take a 5V signal in and provide a 3.3V signal out.) As well this part uses schematic subparts so you can drag each of the 4 gates to a different place in schematic view. Note having many (around 10 or more) subpart parts in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
  SUYIN Audio Jack (TRS) 3.5mm: Stereo Jack 3.5mm
  Neopixel Strip -- White (30/m): These NeoPixel strips have 30 digitally-addressable pixel LEDs per meter and are very affordable and are only 12.5 mm wide, 10 mm if you remove the strip from the casing.
